# Fritzing sketch capstone_project (saved by Fritzing 0.9.4)
breadboards: 1

parts:
  Argon1 = Particle Argon
  Part1 = Adafruit MicroSD card breakout board [part_number="Adafruit #254"]
  Load_Cell1 = Load Cell - Red/white/black/green
  Part2 = HX711 Weighing Sensor Module
  GY2 = MPU-6050 Board GY-521 [form="♀ (female)" package=THT]
  OLED_I2C5 = OLED 128x64 I2C Monochrome Display
  Grove2 = Grove Dust Sensor
  J2 = Basic Servo
  M1 = BMP280
  Part4 = MQ-131 breakout
  MOTOR1 = 28BYJ-48 Stepper Motor
  X2 = X113647 Stepper Driver Board [part_number=X113647 package=board]
  Part5 = 12 NeoPixel Ring [part_number=1643]

nets:
  VCC: Argon1.3.3V, Grove2.VCC, J2.vcc, Part5.VDD
  GND: Argon1.GND, Part1.GND, Grove2.GND, Part5.GND
  N1: Argon1.A0, Grove2.SIG
  N2: Argon1.A2, J2.pulse
  N3: Argon1.A3, Part5.IN
  N4: Argon1.A4, Part4.AO
  N5: Argon1.A5, Part1.CS
  N6: Argon1.SCK, Part1.CLK
  N7: Argon1.MO, Part1.DI
  N8: Argon1.MI, Part1.DO
  N9: Argon1.SDA, GY2.pin4, M1.SDA
  N10: Argon1.SCL, GY2.pin3, OLED_I2C5.SCK, M1.SCL
  N11: Argon1.D2, X2.IN4
  N12: Argon1.D3, X2.IN3
  N13: Argon1.D4, X2.IN2
  N14: Argon1.D5, X2.IN1
  N15: Argon1.D6, Part2.DO/RX
  N16: Argon1.D8, Part2.CK/TX
  N17: Argon1.VUSB, Part1.VCC, X2.+V
  N18: Load_Cell1.wire1, Part2.E+
  N19: Load_Cell1.wire2, Part2.A+
  N20: Load_Cell1.wire3, Part2.E-
  N21: Load_Cell1.wire4, Part2.A-
  VCC_2: Part2.VCC, GY2.pin1, OLED_I2C5.VDD, M1.VIN
  GND_2: Part2.GND, GY2.pin2, OLED_I2C5.GND, M1.GND, X2.GND
  N22: MOTOR1.BLUE, X2.BLUE
  N23: MOTOR1.PINK, X2.PINK
  N24: MOTOR1.RED, X2.YELLOW
  N25: MOTOR1.ORANGE, X2.ORANGE
  N26: MOTOR1.YELLOW, X2.RED

custom parts:
  Particle Argon: The Argon is a powerful Wi-Fi enabled development board that can act as either a standalone Wi-Fi endpoint or Wi-Fi enabled gateway for Particle Mesh networks. It is based on the Nordic nRF52840 and has built-in battery charging circuitry so it’s easy to connect a Li-Po and deploy your local network in minutes. The Argon is great for connecting existing projects to the Particle Device Cloud or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
  Adafruit MicroSD card breakout board: Not just a simple breakout board, this microSD adapter goes the extra mile - designed for ease of use. Onboard 5v->3v regulator provides 150mA for power-hungry cards 3v level shifting means you can use this with ease on either 3v or 5v systems Uses a proper level shifting chip, not resistors: less problems, and faster read/write access Use 3 or 4 digital pins to read and write 2Gb+ of storage!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
  Load Cell - Red/white/black/green: A rectangle load cell/weighting pressure Sensor with four wires - Red, white, black, green. Normally corresponding with E+, E-, A+, A- respectively.
  MPU-6050 Board GY-521: Acelerometro y Giroscopio MPU-6050 Board GY-521
  Grove Dust Sensor: PPD42 Grove Dust Sensor
  BMP280: Temperature Humidity Barometric presure Sensor, I2C
  MQ-131 breakout: SKU: 101282
  28BYJ-48 Stepper Motor: 28BYJ-48 gear-reduction stepper motor (small)
  X113647 Stepper Driver Board: A common stepper motor driver board based on ULN2003APG darlington array
  12 NeoPixel Ring: 12 ultra bright smart LED NeoPixels are arranged in a circle with 1.5" (37mm) outer diameter. The rings are 'chainable' - connect the output pin of one to the input pin of another. Use only one microcontroller pin to control as many as you can chain together! Each LED is addressable as the driver chip is inside the LED. Each one has ~18mA constant current drive so the color will be very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
